# Fritzing sketch Schematic diagram (saved by Fritzing 0.9.6b)
breadboards: 1

parts:
  Mod1 = Arduino Uno WIFI REV2
  Part1 = Adafruit Motor/Stepper/Servo Shield [part_number="Adafruit #1438"]
  M1 = DC Motor
  M2 = DC Motor
  J2 = Basic Servo
  J3 = Basic Servo
  LED1 = smd LED [color="Red (633nm)" package="0805 [SMD]"]  # not connected
  LED2 = smd LED [color="Red (633nm)" package="0603 [SMD]"]  # not connected
  LED3 = smd LED [color="Red (633nm)" package="1206 [SMD]"]  # not connected
  Q1 = PHOTOTRANSISTOR REFLECTIVE OBJECT SENSOR [package=qrb1114-side]
  HC-SR04_Sensor_1 = HC-SR04 Ultrasonic Distance Sensor
  R1 = Resistor [tolerance=±5% power=0.25 resistance=220 package=THT]
  R2 = Resistor [tolerance=±5% power=0.25 resistance=100k package=THT]
  Q3 = PHOTOTRANSISTOR REFLECTIVE OBJECT SENSOR [package=qrb1114-side]
  R3 = Resistor [tolerance=±5% power=0.25 resistance=220 package=THT]
  R4 = Resistor [tolerance=±5% power=0.25 resistance=100k package=THT]

nets:
  5V: Mod1.5V, Mod1.ISCP_5V, HC-SR04_Sensor_1.VCC, R1.Pin_1, R2.Pin_1, R3.Pin_1, R4.Pin_1
  GND: Mod1.GND, Mod1.ISCP_GND, Q1.C, Q1.K, HC-SR04_Sensor_1.GND, Q3.C, Q3.K
  N1: Mod1.D2, Q3.E, R4.Pin_0
  N2: Mod1.D3_PWM, Q3.A, R3.Pin_0
  N3: Mod1.D4, HC-SR04_Sensor_1.TRIG
  N4: Mod1.D5_PWM, HC-SR04_Sensor_1.ECHO
  N5: Part1.M2A, M2.pin_1
  N6: Part1.M2B, M2.pin_2
  N7: Part1.M1B, M1.pin_1
  N8: Part1.M1A, M1.pin_2
  GND_2: Part1.GND, J2.gnd, J3.gnd
  VCC: Part1.+5V, J2.vcc, J3.vcc
  N9: Part1.D10, J3.pulse
  N10: Part1.D9, J2.pulse
  N11: Q1.A, R1.Pin_0
  N12: Q1.E, R2.Pin_0

notes:
  Yellow when moving, red and green for result

custom parts:
  Arduino Uno WIFI REV2: The Arduino Uno WIFI REV2 is a microcontroller board based on the ATmega 4809. It has 14 digital input/output pins (of which 5 can be used as PWM outputs), 6 analog inputs, a 16 MHz ceramic resonator, a USB connection, a power jack, an ICSP header, and a reset button. It also has a WIFI controller with a secure ECC608 crypto unit and an internal IMU. It contains everything needed to support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
  Adafruit Motor/Stepper/Servo Shield: The original Adafruit Motorshield kit is one of our most beloved kits, which is why we decided to make something even better. We have upgraded the shield kit to make the bestest, easiest way to drive DC and Stepper motors. This shield will make quick work of your next robotics project! We kept the ability to drive up to 4 DC motors or 2 stepper motors, but added many improvements: Instead of a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
